# Fritzing sketch Anexo_C_Prototipo_LoRa (saved by Fritzing 1.0.6)
breadboards: 2

parts:
  Componente1 = Arduino Nano (Rev3.0) (ICSP)
  Componente2 = ACS712 Low Current Sensor Board v12
  A1 = AMS11176 module
  MP1584EN_Board1 = MP1584EN Power Regulator Board [part_number=MP1584EN]
  Mod1 = zmpt101b
  U1 = BATTERY-2 [package=battery-aaa]
  Mod2 = KY-019 5V Relay Module [package="Breakout board"]
  Q1 = Basic FET P-Channel [package="D2Pak [SMD]"]
  Q2 = TRANSISTOR_NPN [package=to-92]
  Componente4 = TXB0108 8-channel Bi-directional Logic Level Converter
  LoRa_Module1 = Ra-01 - LoRa Module SX1278 [part_number=SX1278]

nets:
  GND: Componente1.GND, Componente2.GND, A1.pin3, MP1584EN_Board1.OUT_-#13, Mod1.GND, Mod2.-, Componente4.GND, LoRa_Module1.GND
  N1: Componente1.D2, Componente4.B7
  N2: Componente1.D4, Mod2.S
  N3: Componente1.D7, Q2.E
  N4: Componente1.D10, Componente4.B8
  N5: Componente1.D11/MOSI, Componente4.B6
  N6: Componente1.D12/MISO, Componente4.B5
  N7: Componente1.VIN, A1.pin1, MP1584EN_Board1.OUT_-#14, MP1584EN_Board1.OUT_+, Q1.source, Q2.C, Componente4.VCCB
  N8: Componente1.A2, MP1584EN_Board1.IN_+, U1.+1
  N9: Componente1.A1, Mod1.OUT
  N10: Componente1.A0, Componente2.VO
  N11: Componente1.D13/SCK, Componente4.B4
  5V: Componente2.5V, Mod1.VCC, Mod2.+, Q1.drain
  N12: A1.pin2, Componente4.OE, Componente4.VCCA, LoRa_Module1.3.3V
  N13: MP1584EN_Board1.IN_-#10, U1.-1
  N14: Q1.Gate, Q2.B
  N15: Componente4.A8, LoRa_Module1.NSS
  N16: Componente4.A7, LoRa_Module1.DIO0
  N17: Componente4.A5, LoRa_Module1.MISO
  N18: Componente4.A4, LoRa_Module1.SCK

custom parts:
  AMS11176 module: DC-DC step-down modules ( input DC 4.5～7V , output DC 3.3V ).
  MP1584EN Power Regulator Board: The MP1584EN is a high frequency step-down switching regulator. The input voltage range is 4.5V to 28V. The output voltage is set by the board's potentiometer.
  zmpt101b: Single phase ac active output voltate transformer module.
  KY-019 5V Relay Module: KY-019 5V Relay module, used to control AC circuits. (Special thanks to vanepp for fixing the PCB holes and other errors)
  TXB0108 8-channel Bi-directional Logic Level Converter: Because the Arduino (and Basic Stamp) are 5V devices, and most modern sensors, displays, flash cards and modes are 3.3V-only, many makers find that they need to perform level shifting/conversion to protect the 3.3V device from 5V. Although one can use resistors to make a divider, for high speed transfers, the resistors can add a lot of slew and cause havoc that is tough to debug. For that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
  Ra-01 - LoRa Module SX1278: The Ra-01 LoRa Module featuring the SX1278 engine by Semtech. Module by AI-Thinker. Module (Ra-01) specifications from: https://www.banggood.com/Ra-01-Smart-Electronics-SX1278-LoRa-Spread-Spectrum-Wireless-Module-Ultra-Far-10KM-433M-p-1130769.html Description: Power supply: DC1.8-3.7V(3.3V) Chip: SX1278 Frequency: 433Mhz Operating temperature: -40~+85°C On Sheild Description (may vary by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
