# Fritzing sketch Nodo Xbee (saved by Fritzing 1.0.6)
breadboards: 1

parts:
  Componente1 = Arduino Nano (Rev3.0) (ICSP)
  Componente2 = ACS712 Low Current Sensor Board v12
  Componente3 = XBee Pro RF module
  A1 = AMS11176 module
  MP1584EN_Board1 = MP1584EN Power Regulator Board [part_number=MP1584EN]
  Mod1 = zmpt101b
  U1 = BATTERY-2 [package=battery-aaa]
  Mod2 = KY-019 5V Relay Module [package="Breakout board"]
  Q1 = Basic FET P-Channel [package="D2Pak [SMD]"]
  Q2 = TRANSISTOR_NPN [package=to-92]

nets:
  GND: Componente1.GND, Componente2.GND, Componente3.GND, A1.pin3, MP1584EN_Board1.IN_-#9, MP1584EN_Board1.OUT_-#13, Mod1.GND, Mod2.-
  N1: Componente1.D2, Componente3.DOUT
  N2: Componente1.D3, Componente3.DIN
  N3: Componente1.D4, Mod2.S
  N4: Componente1.D7, Q2.E
  N5: Componente1.D9, Componente3.DTR/SLEEP_RQ/DI8
  N6: Componente1.D10, Componente3.ON/SLEEP
  N7: Componente1.VIN, A1.pin1, MP1584EN_Board1.OUT_-#14, MP1584EN_Board1.OUT_+, Q1.source, Q2.C
  N8: Componente1.A2, MP1584EN_Board1.IN_+, U1.+1
  N9: Componente1.A1, Mod1.OUT
  N10: Componente1.A0, Componente2.VO
  5V: Componente2.5V, Mod1.VCC, Mod2.+, Q1.drain
  N11: Componente3.VCC, A1.pin2
  N12: MP1584EN_Board1.IN_-#10, U1.-1
  N13: Q1.Gate, Q2.B

custom parts:
  AMS11176 module: DC-DC step-down modules ( input DC 4.5～7V , output DC 3.3V ).
  MP1584EN Power Regulator Board: The MP1584EN is a high frequency step-down switching regulator. The input voltage range is 4.5V to 28V. The output voltage is set by the board's potentiometer.
  zmpt101b: Single phase ac active output voltate transformer module.
  KY-019 5V Relay Module: KY-019 5V Relay module, used to control AC circuits. (Special thanks to vanepp for fixing the PCB holes and other errors)
